# Fritzing sketch schema (saved by Fritzing 0.9.3b)
breadboards: 1

parts:
  Part1 = Arduino Nano (Rev3.0)
  ZS-042_RTC1 = ZS-042 RTC Module
  L298N1 = L298N DC motor driver
  Part2 = LCD1602-I2C
  R1 = Resistor [tolerance=±5% resistance=400 package="0603 [SMD]"]
  Mod1 = KY-019 5V Relay Module [package="Breakout board"]
  R2 = Resistor [tolerance=±5% resistance=400 package="0603 [SMD]"]
  R3 = Resistor [tolerance=±5% resistance=400 package="0603 [SMD]"]
  R4 = Resistor [tolerance=±5% resistance=400 package="0603 [SMD]"]
  R5 = Resistor [tolerance=±5% resistance=400 package="0603 [SMD]"]
  R6 = Resistor [tolerance=±5% resistance=400 package="0603 [SMD]"]
  U1 = SWITCH_SPDT [package=kps-1290]
  U2 = SWITCH_SPDT [package=kps-1290]
  D2F1 = D2F-FL Omron Snap Action Limit Switch with Level
  D2F2 = D2F-FL Omron Snap Action Limit Switch with Level

nets:
  GND: Part1.GND, ZS-042_RTC1.GND, L298N1.GND, Part2.GND, R1.Pin_0, R2.Pin_0, R3.Pin_0, R4.Pin_0, R5.Pin_0, R6.Pin_0
  N1: Part1.D2, R1.Pin_1, U1.S
  N2: Part1.D3, R2.Pin_1, U1.O
  N3: Part1.D4, R4.Pin_1, U2.S
  N4: Part1.D5, R3.Pin_1, U2.O
  N5: Part1.D6, L298N1.IN2
  N6: Part1.D7, L298N1.IN1
  N7: Part1.D8, R5.Pin_1, D2F2.COM
  N8: Part1.D9, R6.Pin_1, D2F1.COM
  N9: Part1.D12/MISO, Mod1.+
  5V: Part1.5V, ZS-042_RTC1.VCC, L298N1.5V, Part2.VCC, Mod1.S, U1.P, U2.P, D2F1.NO, D2F2.NO
  N10: Part1.A5, ZS-042_RTC1.SCL, Part2.SCL
  N11: Part1.A4, ZS-042_RTC1.SDA, Part2.SDA

custom parts:
  L298N DC motor driver: 2x DC motor driver with 78M05 positive voltage regulator (7..35 V) L298N: max 46 V, 2 A Set 5 V Enable jumper to enable 5 V regultor (needed for the L298N) and +5 V output at screw terminal or supply external +5 V at screw terminal Set ENA and/or ENB to +5 V to enable motor permanently or supply ENA and/or ENB with PWM signal IN1 and IN2 set rotation directory for motor A (OUT1/OUT2) IN2 and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
  LCD1602-I2C: A standard character display, usually with 2x16 characters. Comes in many colors with LCM1602 IIC attached.
  KY-019 5V Relay Module: KY-019 5V Relay module, used to control AC circuits. (Special thanks to vanepp for fixing the PCB holes and other errors)
  D2F-FL Omron Snap Action Limit Switch with Level: Snap action switch with stainless steel lever.
